# Fritzing sketch CoreElectronicsGroup1 (saved by Fritzing 0.9.3b)
circuit board: 13.3cm x 9.6cm
breadboards: 2

parts:
  Geiger1 = RJ11 Jack [package=rj11-6]
  Geiger2 = RJ11 Jack [package=rj11-6]
  GPS = COPERNICUS-DIP [package=copernicus-dip]
  Part3 = Adafruit TSL2561 [part_number="Adafruit #439"]  # not connected
  IMU = 9-DOF Absolute Orientation IMU Fusion Breakout - BNO055
  Part4 = Altitude/Pressure Sensor - MPL3115A2 Breakout [part_number=SEN-11084]  # not connected
  R1 = Resistor [tolerance=±5% resistance=50k package=THT]
  R2 = Resistor [tolerance=±5% resistance=50k package=THT]
  Part5 = Adafruit Feather M0 Adalogger [part_number="Adafruit #2796"]
  J1 = female pin header, 16 pins [form="♀ (female)"]
  J2 = female pin header, 12 pins [form="♀ (female)"]
  5VIN = screw terminal, 2 pins
  L3Power = screw terminal, 2 pins
  L3Signal = screw terminal, 2 pins
  PressureSensorPower = screw terminal, 2 pins
  PressureSensorSignal = screw terminal, 2 pins
  CutoffSignal = screw terminal, 2 pins
  L1Power = screw terminal, 2 pins
  L1Signal = screw terminal, 2 pins
  L2Power = screw terminal, 2 pins
  L2Signal = screw terminal, 2 pins
  5Vto3V3StepDown = Adafruit LM3671 Buck Converter [part_number="Adafruit #2745"]
  CutoffRelay = Adafruit Mini Relay FeatherWing [part_number="Adafruit #2895"]

nets:
  N1: Geiger1.2, Geiger2.2, R1.Pin_1, R2.Pin_1
  N2: Geiger1.3, Part5.D11, J2.pin6
  3.3V: Geiger1.4, Geiger2.4, GPS.VCC, GPS.XSTANDBY, IMU.5.0V, R2.Pin_0, L3Power.pin2, PressureSensorPower.pin2, L1Power.pin2, L2Power.pin2, 5Vto3V3StepDown.3.3V, CutoffRelay.3.3V
  GND: Geiger1.5, Geiger2.5, GPS.OPEN, GPS.GND, IMU.GND, R1.Pin_0, Part5.GND, J1.pin4, J1.pin16, 5VIN.pin1, L3Power.pin1, PressureSensorPower.pin1, L1Power.pin1, L2Power.pin1, 5Vto3V3StepDown.GND, CutoffRelay.GND
  N3: Geiger2.3, Part5.D12, J2.pin5
  N4: GPS.TXD-B, Part5.D0, J1.pin14
  N5: IMU.SDA_5V, Part5.SDA, J2.pin12, L3Signal.pin2, PressureSensorSignal.pin2, L1Signal.pin2, L2Signal.pin2
  N6: IMU.SCL_5V, Part5.SCL, J2.pin11, L3Signal.pin1, PressureSensorSignal.pin1, L1Signal.pin1, L2Signal.pin1
  N7: Part5.D1, J1.pin15
  N8: Part5.MISO, J1.pin13
  N9: Part5.MOSI, J1.pin12
  N10: Part5.SCK, J1.pin11
  N11: Part5.A5, J1.pin10
  N12: Part5.A4, J1.pin9
  N13: Part5.A3, J1.pin8
  N14: Part5.A2, J1.pin7
  N15: Part5.A1, J1.pin6
  N16: Part5.A0, J1.pin5
  N17: Part5.AREF, J1.pin3
  N18: Part5.+3V3, J1.pin2
  N19: Part5.!RESET, J1.pin1
  N20: Part5.VBAT, J2.pin1
  N21: Part5.EN, J2.pin2
  N22: Part5.VBUS, J2.pin3
  N23: Part5.D13, J2.pin4
  N24: Part5.D10, J2.pin7
  N25: Part5.D9, J2.pin8
  N26: Part5.D6, J2.pin9
  N27: Part5.D5, J2.pin10
  N28: 5VIN.pin2, 5Vto3V3StepDown.EN, 5Vto3V3StepDown.VIN
  N29: CutoffSignal.pin1, CutoffRelay.SIGNAL

notes:
  RMC PH549
  Eye of the
  Geiger
  GPS
  IMU
  Feather M0
  Relay
  L2SCL
  L2SDA
  GND
  3V3
  L1SCL
  L1SDA
  CUTOFF
  PrSCL
  PrSDA
  L3SDA
  L3SCL
  5VIN
  50k

custom parts:
  Adafruit TSL2561: The TSL2561 luminosity sensor is an advanced digital light sensor, ideal for use in a wide range of light situations. Compared to low cost CdS cells, this sensor is more precise, allowing for exact lux calculations and can be configured for different gain/timing ranges to detect light ranges from up to 0.1 - 40,000+ Lux on the fly. The best part of this sensor is that it contains both infrared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
  9-DOF Absolute Orientation IMU Fusion Breakout - BNO055: A MEMS accelerometer, magnetometer and gyroscope on a single die with a high speed ARM Cortex-M0 based processor to digest all the sensor data, abstract the sensor fusion and real time requirements away, and spit out data you can use in quaternions, Euler angles or vectors.
  Adafruit Feather M0 Adalogger: This is the Adafruit Feather M0 Adalogger - our take on an 'all-in-one' Cortex M0 datalogger (or data-reader) with built in USB and battery charging. Its an Adafruit Feather M0 with a microSD holder ready to rock! We have other boards in the Feather family, check'em out here At the Feather M0's heart is an ATSAMD21G18 ARM Cortex M0 processor, clocked at 48 MHz and at 3.3V logic, the same one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
  Adafruit LM3671 Buck Converter: Your power supply problems just got SUPER SOLVED! This 3.3V Buck Converter Breakout board is great for supplying power to low voltage circuits from a single Li-Ion cell battery or USB power. This chip provides up to 600-mA load current across the entire input voltage range of 3.5 to 5.5V. Great for your portable project, we made this "pin compatible" with the LM1117-3.3V TO-220 chip so you can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
  Adafruit Mini Relay FeatherWing: A Feather board without ambition is a Feather board without FeatherWings! This is the Non-Latching Mini Relay FeatherWing. It gives you power to control, and control over power. Put simply, you can now turn on and off lamps, fans, solenoids, and other small appliances that run on up to 250VAC or DC power using any Feather board. The are two 'flavors' of these FeatherWings, this is the simple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
