# Fritzing sketch CoreElectronicsGroup1FinalPCB (saved by Fritzing 0.9.3b)
circuit board: 13.3cm x 9.6cm
breadboards: 2

parts:
  Geiger1 = RJ11 Jack [package=rj11-6]
  Geiger2 = RJ11 Jack [package=rj11-6]
  Part3 = Adafruit TSL2561 [part_number="Adafruit #439"]  # not connected
  IMU = 9-DOF Absolute Orientation IMU Fusion Breakout - BNO055
  Part4 = Altitude/Pressure Sensor - MPL3115A2 Breakout [part_number=SEN-11084]  # not connected
  50k = Resistor [tolerance=±5% resistance=50k package=THT]
  50k_2 = Resistor [tolerance=±5% resistance=50k package=THT]
  Feather_M0 = Adafruit Feather M0 Adalogger [part_number="Adafruit #2796"]
  part = female pin header, 16 pins [form="♀ (female)"]
  part_2 = female pin header, 12 pins [form="♀ (female)"]
  part_3 = screw terminal, 2 pins
  part_4 = screw terminal, 2 pins
  part_5 = screw terminal, 2 pins
  part_6 = screw terminal, 2 pins
  part_7 = screw terminal, 2 pins
  part_8 = screw terminal, 2 pins
  part_9 = screw terminal, 2 pins
  part_10 = screw terminal, 2 pins
  part_11 = screw terminal, 2 pins
  part_12 = screw terminal, 2 pins
  5V3V3 = female pin header, 4 pins [form="♀ (female)"]
  part_13 = female pin header, 16 pins [form="♀ (female)"]
  part_14 = female pin header, 12 pins [form="♀ (female)"]  # not connected
  part_15 = female pin header, 1 pin [form="♀ (female)"]
  J8 = female pin header, 10 pins [form="♀ (female)"]  # not connected
  J7 = rounded female pin header, 10 pins [form="♀ (female rounded)"]

nets:
  N1: Geiger1.2, Geiger2.2, 50k.Pin_1, 50k_2.Pin_1
  N2: Geiger1.3, Feather_M0.D11, part_2.pin6
  N3: Geiger1.4, Geiger2.4, IMU.5.0V, 50k_2.Pin_0, part_4.pin2, part_6.pin2, part_9.pin2, part_11.pin2, 5V3V3.pin3, part_13.pin15, J7.pin8, J7.pin10
  GND: Geiger1.5, Geiger2.5, IMU.GND, 50k.Pin_0, Feather_M0.GND, part.pin4, part.pin16, part_3.pin1, part_4.pin1, part_6.pin1, part_9.pin1, part_11.pin1, 5V3V3.pin4, part_13.pin13, J7.pin3, J7.pin9
  N4: Geiger2.3, Feather_M0.D12, part_2.pin5
  N5: IMU.SDA_5V, Feather_M0.SDA, part_2.pin12, part_5.pin2, part_7.pin2, part_10.pin2, part_12.pin2
  N6: IMU.SCL_5V, Feather_M0.SCL, part_2.pin11, part_5.pin1, part_7.pin1, part_10.pin1, part_12.pin1
  N7: Feather_M0.D1, part.pin15
  N8: Feather_M0.D0, part.pin14
  N9: Feather_M0.MISO, part.pin13
  N10: Feather_M0.MOSI, part.pin12
  N11: Feather_M0.SCK, part.pin11
  N12: Feather_M0.A5, part.pin10
  N13: Feather_M0.A4, part.pin9
  N14: Feather_M0.A3, part.pin8
  N15: Feather_M0.A2, part.pin7
  N16: Feather_M0.A1, part.pin6
  N17: Feather_M0.A0, part.pin5
  N18: Feather_M0.AREF, part.pin3
  N19: Feather_M0.+3V3, part.pin2
  N20: Feather_M0.!RESET, part.pin1
  N21: Feather_M0.VBAT, part_2.pin1
  N22: Feather_M0.EN, part_2.pin2
  N23: Feather_M0.VBUS, part_2.pin3
  N24: Feather_M0.D13, part_2.pin4
  N25: Feather_M0.D10, part_2.pin7
  N26: Feather_M0.D9, part_2.pin8
  N27: Feather_M0.D6, part_2.pin9
  N28: Feather_M0.D5, part_2.pin10
  N29: part_3.pin2, 5V3V3.pin1, 5V3V3.pin2
  N30: part_8.pin1, part_15.pin1

notes:
  RMC PH549
  Eye of the
  Geiger
  GPS
  Relay
  L2SCL
  L2SDA
  GND
  3V3
  L1SCL
  L1SDA
  CUTOFF
  PrSCL
  PrSDA
  L3SDA
  L3SCL
  5VIN
  LM3671

custom parts:
  Adafruit TSL2561: The TSL2561 luminosity sensor is an advanced digital light sensor, ideal for use in a wide range of light situations. Compared to low cost CdS cells, this sensor is more precise, allowing for exact lux calculations and can be configured for different gain/timing ranges to detect light ranges from up to 0.1 - 40,000+ Lux on the fly. The best part of this sensor is that it contains both infrared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
  9-DOF Absolute Orientation IMU Fusion Breakout - BNO055: A MEMS accelerometer, magnetometer and gyroscope on a single die with a high speed ARM Cortex-M0 based processor to digest all the sensor data, abstract the sensor fusion and real time requirements away, and spit out data you can use in quaternions, Euler angles or vectors.
  Adafruit Feather M0 Adalogger: This is the Adafruit Feather M0 Adalogger - our take on an 'all-in-one' Cortex M0 datalogger (or data-reader) with built in USB and battery charging. Its an Adafruit Feather M0 with a microSD holder ready to rock! We have other boards in the Feather family, check'em out here At the Feather M0's heart is an ATSAMD21G18 ARM Cortex M0 processor, clocked at 48 MHz and at 3.3V logic, the same one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
