# Fritzing sketch CoreElectronicsGroup1Schematic (saved by Fritzing 0.9.3b)
circuit board: 13.3cm x 9.6cm
breadboards: 2

parts:
  Geiger1 = RJ11 Jack [package=rj11-6]
  Geiger2 = RJ11 Jack [package=rj11-6]
  GPS = COPERNICUS-DIP [package=copernicus-dip]
  Part3 = Adafruit TSL2561 [part_number="Adafruit #439"]
  IMU = 9-DOF Absolute Orientation IMU Fusion Breakout - BNO055
  R1 = Resistor [tolerance=±5% resistance=50k package=THT]
  R2 = Resistor [tolerance=±5% resistance=50k package=THT]
  Part5 = Adafruit Feather M0 Adalogger [part_number="Adafruit #2796"]
  5Vto3V3StepDown = Adafruit LM3671 Buck Converter [part_number="Adafruit #2745"]
  CutoffRelay = Adafruit Mini Relay FeatherWing [part_number="Adafruit #2895"]
  Part4 = Altitude/Pressure Sensor - MPL3115A2 Breakout [part_number=SEN-11084]  # not connected
  Part6 = Adafruit TSL2561 [part_number="Adafruit #439"]
  Part7 = Adafruit TSL2561 [part_number="Adafruit #439"]
  J1 = Screw terminal - 2 pins [package=THT]
  J2 = Screw terminal - 2 pins [package=THT]

nets:
  N1: Geiger1.2, Geiger2.2, R1.Pin_1, R2.Pin_1
  N2: Geiger1.3, Part5.D11
  VIN: Geiger1.4, Geiger2.4, GPS.VCC, GPS.XSTANDBY, Part3.VIN, IMU.5.0V, R2.Pin_0, 5Vto3V3StepDown.3.3V, CutoffRelay.3.3V, Part6.VIN, Part7.VIN, Part7.ADDR
  GND: Geiger1.5, Geiger2.5, GPS.OPEN, GPS.GND, Part3.GND, IMU.GND, R1.Pin_0, Part5.GND, 5Vto3V3StepDown.GND, CutoffRelay.GND, Part6.GND, Part6.ADDR, Part7.GND, J1.pin2
  N3: Geiger2.3, Part5.D12
  N4: GPS.RXD-B, Part5.D1
  N5: GPS.TXD-B, Part5.D0
  N6: Part3.SDA, IMU.SDA_5V, Part5.SDA, Part6.SDA, Part7.SDA
  N7: Part3.SCL, IMU.SCL_5V, Part5.SCL, Part6.SCL, Part7.SCL
  N8: 5Vto3V3StepDown.EN, 5Vto3V3StepDown.VIN, J1.pin1
  N9: CutoffRelay.SIGNAL, CutoffRelay.EN, J2.pin2
  N10: CutoffRelay.USB, J2.pin1

notes:
  RMC PH549
  Eye of the
  Geiger
  GPS
  IMU
  Feather M0
  Relay
  L2SCL
  L2SDA
  GND
  3V3
  L1SCL
  L1SDA
  CUTOFF
  PrSCL
  PrSDA
  L3SDA
  L3SCL
  5VIN
  50k

custom parts:
  Adafruit TSL2561: The TSL2561 luminosity sensor is an advanced digital light sensor, ideal for use in a wide range of light situations. Compared to low cost CdS cells, this sensor is more precise, allowing for exact lux calculations and can be configured for different gain/timing ranges to detect light ranges from up to 0.1 - 40,000+ Lux on the fly. The best part of this sensor is that it contains both infrared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
  9-DOF Absolute Orientation IMU Fusion Breakout - BNO055: A MEMS accelerometer, magnetometer and gyroscope on a single die with a high speed ARM Cortex-M0 based processor to digest all the sensor data, abstract the sensor fusion and real time requirements away, and spit out data you can use in quaternions, Euler angles or vectors.
  Adafruit Feather M0 Adalogger: This is the Adafruit Feather M0 Adalogger - our take on an 'all-in-one' Cortex M0 datalogger (or data-reader) with built in USB and battery charging. Its an Adafruit Feather M0 with a microSD holder ready to rock! We have other boards in the Feather family, check'em out here At the Feather M0's heart is an ATSAMD21G18 ARM Cortex M0 processor, clocked at 48 MHz and at 3.3V logic, the same one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
  Adafruit LM3671 Buck Converter: Your power supply problems just got SUPER SOLVED! This 3.3V Buck Converter Breakout board is great for supplying power to low voltage circuits from a single Li-Ion cell battery or USB power. This chip provides up to 600-mA load current across the entire input voltage range of 3.5 to 5.5V. Great for your portable project, we made this "pin compatible" with the LM1117-3.3V TO-220 chip so you can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
  Adafruit Mini Relay FeatherWing: A Feather board without ambition is a Feather board without FeatherWings! This is the Non-Latching Mini Relay FeatherWing. It gives you power to control, and control over power. Put simply, you can now turn on and off lamps, fans, solenoids, and other small appliances that run on up to 250VAC or DC power using any Feather board. The are two 'flavors' of these FeatherWings, this is the simple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
